# Fritzing sketch Led_RGB (saved by Fritzing 0.9.3b)
breadboards: 1

parts:
  Componente1 = Arduino Uno (Rev3)
  R2 = Resistor [tolerance=±5% resistance=220 package=THT]
  R3 = Resistor [tolerance=±5% resistance=220 package=THT]
  R4 = Resistor [tolerance=±5% resistance=220 package=THT]
  LED1 = RGB LED (com. cathode, rgb) [package="5 mm [THT]"]

nets:
  N1: Componente1.D10_PWM/SS, R4.Pin_1
  N2: Componente1.D11_PWM/MOSI, R2.Pin_1
  N3: Componente1.GND, LED1.red_anode
  N4: R2.Pin_0, LED1.common_cathode
  N5: R3.Pin_0, LED1.blue_anode
  N6: R4.Pin_0, LED1.green_anode
